// Logisim project clock.circ as structural Verilog: 3 circuits, main circuit clock logic
module clock_logic (
  input  u,
  input  v,
  input  w,
  input  x,
  output a,
  output b,
  output c,
  output d,
  output e,
  output f,
  output g
);

  wire and_1_out, and_2_out, and_3_out, and_4_out, and_5_out, and_6_out, and_7_out, and_8_out, and_9_out,
       and_10_out, and_11_out, and_12_out, and_13_out, and_14_out, and_15_out, and_16_out, and_17_out,
       and_18_out, and_19_out, and_20_out, and_21_out, and_22_out, and_23_out, and_24_out, and_25_out,
       and_26_out, not_1_out, not_2_out, not_3_out, not_4_out, or_1_out, or_2_out, or_3_out, or_4_out,
       or_5_out, or_6_out, or_7_out, or_8_out, or_9_out, or_10_out, or_12_out, or_14_out, or_16_out,
       or_18_out;

  not not_1 (not_1_out, u);
  not not_2 (not_2_out, v);
  not not_3 (not_3_out, w);
  not not_4 (not_4_out, x);
  and and_1 (and_1_out, not_2_out, not_4_out);
  and and_2 (and_2_out, v, x);
  and and_3 (and_3_out, not_1_out, not_3_out);
  and and_4 (and_4_out, not_1_out, w);
  and and_5 (and_5_out, not_2_out, not_3_out);
  and and_6 (and_6_out, not_1_out, x);
  and and_7 (and_7_out, not_2_out, not_4_out);
  and and_8 (and_8_out, not_2_out, w);
  and and_9 (and_9_out, v, not_3_out);
  and and_10 (and_10_out, not_2_out, not_4_out);
  and and_11 (and_11_out, w, not_4_out);
  and and_12 (and_12_out, u, w);
  and and_13 (and_13_out, u, v);
  and and_14 (and_14_out, not_3_out, not_4_out);
  and and_15 (and_15_out, v, not_3_out);
  and and_16 (and_16_out, v, not_4_out);
  and and_17 (and_17_out, not_2_out, w);
  and and_18 (and_18_out, v, not_3_out);
  and and_19 (and_19_out, v, not_4_out);
  or or_1 (or_1_out, and_1_out, w);
  or or_2 (or_2_out, and_2_out, u);
  and and_20 (and_20_out, not_1_out, not_2_out);
  and and_21 (and_21_out, and_3_out, not_4_out);
  and and_22 (and_22_out, not_2_out, not_3_out);
  and and_23 (and_23_out, and_4_out, x);
  or or_3 (or_3_out, and_5_out, and_6_out);
  and and_24 (and_24_out, not_1_out, v);
  or or_4 (or_4_out, and_7_out, and_8_out);
  and and_25 (and_25_out, w, not_4_out);
  and and_26 (and_26_out, and_9_out, x);
  or or_5 (or_5_out, and_10_out, and_11_out);
  or or_6 (or_6_out, and_12_out, and_13_out);
  or or_7 (or_7_out, and_14_out, and_15_out);
  or or_8 (or_8_out, and_16_out, u);
  or or_9 (or_9_out, and_17_out, and_18_out);
  or or_10 (or_10_out, and_19_out, u);
  or or_11 (a, or_1_out, or_2_out);
  or or_12 (or_12_out, and_20_out, and_21_out);
  or or_13 (b, or_12_out, or_14_out);
  or or_14 (or_14_out, and_22_out, and_23_out);
  or or_15 (c, or_3_out, and_24_out);
  or or_16 (or_16_out, or_4_out, and_25_out);
  or or_17 (d, or_16_out, or_18_out);
  or or_18 (or_18_out, and_26_out, u);
  or or_19 (e, or_5_out, or_6_out);
  or or_20 (f, or_7_out, or_8_out);
  or or_21 (g, or_9_out, or_10_out);
endmodule

module clock_circuit (
  input  clock,
  output _1a,
  output _1b,
  output _1c,
  output _1d,
  output _1e,
  output _1f,
  output _1g,
  output _2a,
  output _2b,
  output _2c,
  output _2d,
  output _2e,
  output _2f,
  output _2g
);

  wire and_1_out, and_2_out, and_3_out, and_4_out, not_1_out, not_2_out, not_3_out;
  wire [3:0] counter_2_q, counter_3_q, counter_4_q;
  wire [5:0] counter_1_q;

  Counter #(.width(6), .max('h3f)) counter_1 (
    .Q(counter_1_q), .clk(clock), .clr(and_1_out));  // open: load, D, count, carry
  not not_1 (not_1_out, counter_1_q[2]);
  not not_2 (not_2_out, counter_2_q[1]);
  Counter #(.width(4), .max('hf)) counter_2 (
    .Q(counter_2_q), .clk(and_1_out), .clr(and_2_out));  // open: load, D, count, carry
  not not_3 (not_3_out, counter_2_q[2]);
  and and_1 (and_1_out, counter_1_q[0], counter_1_q[1], not_1_out, counter_1_q[3], counter_1_q[4], counter_1_q[5]);
  and and_2 (and_2_out, counter_2_q[0], not_2_out, not_3_out, counter_2_q[3]);
  Counter #(.width(4), .max('hf)) counter_3 (
    .Q(counter_3_q), .clk(and_1_out), .clr(and_3_out));  // open: load, D, count, carry
  and and_3 (and_3_out, counter_3_q[3], counter_3_q[1]);
  Counter #(.width(4), .max('hf)) counter_4 (
    .Q(counter_4_q), .clk(and_2_out), .clr(and_4_out));  // open: load, D, count, carry
  and and_4 (and_4_out, counter_4_q[3], counter_4_q[1]);
  clock_logic clock_logic_1 (
    .u(counter_3_q[3]), .v(counter_3_q[2]), .w(counter_3_q[1]), .x(counter_3_q[0]), .a(_1a), .b(_1b),
    .c(_1c), .d(_1d), .e(_1e), .f(_1f), .g(_1g));
  clock_logic clock_logic_2 (
    .u(counter_4_q[3]), .v(counter_4_q[2]), .w(counter_4_q[1]), .x(counter_4_q[0]), .a(_2a), .b(_2b),
    .c(_2c), .d(_2d), .e(_2e), .f(_2f), .g(_2g));
endmodule

module main (
);

  wire clock_1_out, clock_circuit_1__1a, clock_circuit_1__1b, clock_circuit_1__1c, clock_circuit_1__1d,
       clock_circuit_1__1e, clock_circuit_1__1f, clock_circuit_1__1g, clock_circuit_1__2a,
       clock_circuit_1__2b, clock_circuit_1__2c, clock_circuit_1__2d, clock_circuit_1__2e,
       clock_circuit_1__2f, clock_circuit_1__2g;

  _7_Segment_Display u_7_segment_display_1 (
    .g(clock_circuit_1__1g), .f(clock_circuit_1__1f), .a(clock_circuit_1__1a), .b(clock_circuit_1__1b),
    .e(clock_circuit_1__1e), .d(clock_circuit_1__1d), .c(clock_circuit_1__1c));  // open: dp
  clock_circuit clock_circuit_1 (
    .clock(clock_1_out), ._1a(clock_circuit_1__1a), ._1b(clock_circuit_1__1b), ._1c(clock_circuit_1__1c),
    ._1d(clock_circuit_1__1d), ._1e(clock_circuit_1__1e), ._1f(clock_circuit_1__1f),
    ._1g(clock_circuit_1__1g), ._2a(clock_circuit_1__2a), ._2b(clock_circuit_1__2b),
    ._2c(clock_circuit_1__2c), ._2d(clock_circuit_1__2d), ._2e(clock_circuit_1__2e),
    ._2f(clock_circuit_1__2f), ._2g(clock_circuit_1__2g));
  Clock clock_1 (.out(clock_1_out));
  _7_Segment_Display u_7_segment_display_2 (
    .g(clock_circuit_1__2g), .f(clock_circuit_1__2f), .a(clock_circuit_1__2a), .b(clock_circuit_1__2b),
    .e(clock_circuit_1__2e), .d(clock_circuit_1__2d), .c(clock_circuit_1__2c));  // open: dp
endmodule
