// Logisim project gelo.circ as structural Verilog: 1 circuit, main circuit main
module main (
  input  in_1,
  input  in_2,
  input  in_3,
  input  in_4,
  input  in_5,
  input  in_6,
  input  in_7,
  input  in_8
);

  _7_Segment_Display u_7_segment_display_1 (.g(in_1), .f(in_1), .a(in_1), .e(in_1));  // open: b, d, c, dp
  _7_Segment_Display u_7_segment_display_2 (.f(in_5), .a(in_5), .e(in_5), .d(in_5), .c(in_5));  // open: g, b, dp
  _7_Segment_Display u_7_segment_display_3 (.f(in_2), .b(in_2), .e(in_2), .d(in_2), .c(in_2));  // open: g, a, dp
  _7_Segment_Display u_7_segment_display_4 (.g(in_6), .f(in_6), .a(in_6), .e(in_6), .d(in_6));  // open: b, c, dp
  _7_Segment_Display u_7_segment_display_5 (.f(in_3), .a(in_3), .e(in_3), .d(in_3));  // open: g, b, c, dp
  _7_Segment_Display u_7_segment_display_6 (.f(in_7), .e(in_7), .d(in_7));  // open: g, a, b, c, dp
  _7_Segment_Display u_7_segment_display_7 (.f(in_4), .b(in_4), .e(in_4), .d(in_4), .c(in_4));  // open: g, a, dp
  _7_Segment_Display u_7_segment_display_8 (.f(in_8), .a(in_8), .b(in_8), .e(in_8), .d(in_8), .c(in_8));  // open: g, dp
endmodule
